// Digital circuit full_sum.dig as structural Verilog
module full_sum (
  input  a0,
  input  a2,
  input  a1,
  input  a3,
  input  b0,
  input  b1,
  input  b2,
  input  b3,
  input  Cin,
  output s0,
  output s1,
  output s2,
  output s3,
  output Cout
);

  wire u_sum0_cout, u_sum1_cout, u_sum2_cout;

  sum0 #(.applicationType("IVERILOG"), .CodeFile("/home/alejandro/Documents/gits/Digital-UN-2023_2/lab_sum/sum.v")) u_sum0 (
    .B(b0), .A(a0), .Cin(Cin), .Cout(u_sum0_cout), .S(s0));
  sum1 #(.applicationType("IVERILOG"), .CodeFile("/home/alejandro/Documents/gits/Digital-UN-2023_2/lab_sum/sum.v")) u_sum1 (
    .B(b1), .A(a1), .Cin(u_sum0_cout), .Cout(u_sum1_cout), .S(s1));
  sum2 #(.applicationType("IVERILOG"), .CodeFile("/home/alejandro/Documents/gits/Digital-UN-2023_2/lab_sum/sum.v")) u_sum2 (
    .B(b2), .A(a2), .Cin(u_sum1_cout), .Cout(u_sum2_cout), .S(s2));
  sum3 #(.applicationType("IVERILOG"), .CodeFile("/home/alejandro/Documents/gits/Digital-UN-2023_2/lab_sum/sum.v")) u_sum3 (
    .B(b3), .A(a3), .Cin(u_sum2_cout), .Cout(Cout), .S(s3));
endmodule
