// Digital circuit sum.dig as structural Verilog
module sum (
  input  B,
  input  A,
  input  Cin,
  output Cout,
  output S
);

  wire and_1_out, and_2_out, or_1_out, xor_1_out;

  and and_1 (and_1_out, A, B);
  or or_1 (or_1_out, B, A);
  xor xor_1 (xor_1_out, B, A);
  and and_2 (and_2_out, or_1_out, Cin);
  or or_2 (Cout, and_1_out, and_2_out);
  xor xor_2 (S, xor_1_out, Cin);
endmodule
