// Digital circuit SumRes.dig as structural Verilog
module SumRes (
  input  a0,
  input  a2,
  input  a1,
  input  a3,
  input  b0,
  input  b1,
  input  b2,
  input  b3,
  input  Op
);

  wire not_1_out, u_bcd7seg_hex_a, u_bcd7seg_hex_b, u_bcd7seg_hex_c, u_bcd7seg_hex_d, u_bcd7seg_hex_e,
       u_bcd7seg_hex_f, u_bcd7seg_hex_g, u_sum_2_cout, u_sum_2_s, u_sum_3_cout, u_sum_3_s, u_sum_4_s,
       u_sum_cout, u_sum_s, xor_1_out, xor_2_out, xor_3_out, xor_4_out;

  xor xor_1 (xor_1_out, b0, Op);
  xor xor_2 (xor_2_out, b1, Op);
  xor xor_3 (xor_3_out, b2, Op);
  xor xor_4 (xor_4_out, b3, Op);
  sum #(.applicationType("IVERILOG"), .CodeFile("/home/v/Descargas/SumRes/sum.v")) u_sum (
    .B(xor_1_out), .A(a0), .Cin(Op), .Cout(u_sum_cout), .S(u_sum_s));
  sum #(.applicationType("IVERILOG"), .CodeFile("/home/v/Descargas/SumRes/sum.v")) u_sum_2 (
    .B(xor_2_out), .A(a1), .Cin(u_sum_cout), .Cout(u_sum_2_cout), .S(u_sum_2_s));
  sum #(.applicationType("IVERILOG"), .CodeFile("/home/v/Descargas/SumRes/sum.v")) u_sum_3 (
    .B(xor_3_out), .A(a2), .Cin(u_sum_2_cout), .Cout(u_sum_3_cout), .S(u_sum_3_s));
  sum #(.applicationType("IVERILOG"), .CodeFile("/home/v/Descargas/SumRes/sum.v")) u_sum_4 (
    .B(xor_4_out), .A(a3), .Cin(u_sum_3_cout), .S(u_sum_4_s));  // open: Cout
  not not_1 (not_1_out, 1'b0);
  bcd7seg_hex #(.applicationType("IVERILOG"), .CodeFile("/home/v/Descargas/SumRes/bcd7seg_hex.v")) u_bcd7seg_hex (
    .a1(u_sum_4_s), .b1(u_sum_3_s), .c1(u_sum_2_s), .d1(u_sum_s), .a(u_bcd7seg_hex_a), .b(u_bcd7seg_hex_b),
    .c(u_bcd7seg_hex_c), .d(u_bcd7seg_hex_d), .e(u_bcd7seg_hex_e), .f(u_bcd7seg_hex_f), .g(u_bcd7seg_hex_g));
  Seven_Seg #(.commonCathode("true"), .commonConnectionType("anode")) seven_seg_1 (
    .a(u_bcd7seg_hex_a), .b(u_bcd7seg_hex_b), .c(u_bcd7seg_hex_c), .d(u_bcd7seg_hex_d), .e(u_bcd7seg_hex_e),
    .f(u_bcd7seg_hex_f), .g(u_bcd7seg_hex_g), .dp(not_1_out), .common(1'b1));
endmodule
