// Digital circuit digitalBCDto7seg.dig as structural Verilog
module digitalBCDto7seg (
  input  in_1,
  input  in_2,
  input  in_3,
  input  in_4
);

  wire u_bcd7seg_a, u_bcd7seg_b, u_bcd7seg_c, u_bcd7seg_d, u_bcd7seg_e, u_bcd7seg_f, u_bcd7seg_g;

  bcd7seg #(.applicationType("IVERILOG"), .CodeFile("bcd7seg.v")) u_bcd7seg (
    .a1(in_1), .b1(in_2), .c1(in_3), .d1(in_4), .a(u_bcd7seg_a), .b(u_bcd7seg_b), .c(u_bcd7seg_c),
    .d(u_bcd7seg_d), .e(u_bcd7seg_e), .f(u_bcd7seg_f), .g(u_bcd7seg_g));
  Seven_Seg #(.commonCathode("true"), .commonConnectionType("anode")) seven_seg_1 (
    .a(u_bcd7seg_a), .b(u_bcd7seg_b), .c(u_bcd7seg_c), .d(u_bcd7seg_d), .e(u_bcd7seg_e), .f(u_bcd7seg_f),
    .g(u_bcd7seg_g), .dp(1'b1), .common(1'b1));
endmodule
