// Digital circuit full_sum.dig as structural Verilog
module full_sum (
  input  a0,
  input  a2,
  input  a1,
  input  a3,
  input  b0,
  input  b1,
  input  b2,
  input  b3,
  input  Cin,
  output s0,
  output s1,
  output s2,
  output s3,
  output s4
);

  wire u_sum_2_cout, u_sum_3_cout, u_sum_cout;

  sum #(.applicationType("IVERILOG"), .CodeFile("/home/alejandro/Documents/gits/Digital-UN-2023_2/lab_sum/sum.v")) u_sum (
    .B(b0), .A(a0), .Cin(Cin), .Cout(u_sum_cout), .S(s0));
  sum #(.applicationType("IVERILOG"), .CodeFile("/home/alejandro/Documents/gits/Digital-UN-2023_2/lab_sum/sum.v")) u_sum_2 (
    .B(b1), .A(a1), .Cin(u_sum_cout), .Cout(u_sum_2_cout), .S(s1));
  sum #(.applicationType("IVERILOG"), .CodeFile("/home/alejandro/Documents/gits/Digital-UN-2023_2/lab_sum/sum.v")) u_sum_3 (
    .B(b2), .A(a2), .Cin(u_sum_2_cout), .Cout(u_sum_3_cout), .S(s2));
  sum #(.applicationType("IVERILOG"), .CodeFile("/home/alejandro/Documents/gits/Digital-UN-2023_2/lab_sum/sum.v")) u_sum_4 (
    .B(b3), .A(a3), .Cin(u_sum_3_cout), .Cout(s4), .S(s3));
endmodule
