// Digital circuit full_sum_4bit.dig as structural Verilog
module full_sum_4bit (
  input  a0,
  input  a2,
  input  a1,
  input  a3,
  input  b0,
  input  b1,
  input  b2,
  input  b3,
  input  Cin,
  output Cout,
  output a,
  output b,
  output c,
  output d,
  output e,
  output f,
  output g
);

  wire full_sum_1_s0, full_sum_1_s1, full_sum_1_s2, full_sum_1_s3;

  full_sum full_sum_1 (
    .a0(a0), .a2(a1), .a1(a2), .a3(a3), .b0(b0), .b1(b1), .b2(b2), .b3(b3), .Cin(Cin), .s0(full_sum_1_s0),
    .s1(full_sum_1_s1), .s2(full_sum_1_s2), .s3(full_sum_1_s3), .s4(Cout));
  bcd7seg_hex #(.applicationType("IVERILOG"), .CodeFile("/home/alejandro/Documents/gits/Digital-UN-2023_2/lab_sum/bcd7seg_hex.v")) u_bcd7seg_hex (
    .a1(full_sum_1_s0), .b1(full_sum_1_s1), .c1(full_sum_1_s2), .d1(full_sum_1_s3), .a(a), .b(b), .c(c),
    .d(d), .e(e), .f(f), .g(g));
endmodule
