// Digital circuit sum7seg_hex.dig as structural Verilog
module sum7seg_hex (
  input  in_1,
  input  in_2,
  input  in_3,
  input  in_4,
  input  in_5,
  input  in_6,
  input  in_7,
  input  in_8,
  input  in_9
);

  wire u_sum7sec_hex_led_a, u_sum7sec_hex_led_b, u_sum7sec_hex_led_c, u_sum7sec_hex_led_d,
       u_sum7sec_hex_led_e, u_sum7sec_hex_led_f, u_sum7sec_hex_led_g, u_sum7sec_hex_led_h;

  sum7sec_hex #(.applicationType("IVERILOG"), .CodeFile("/home/alejandro/Documents/gits/Digital-UN-2023_2/lab_sum/sum7sec_hex.v")) u_sum7sec_hex (
    .x0(in_1), .x1(in_2), .x2(in_4), .x3(in_3), .y0(in_5), .y1(in_6), .y2(in_7), .y3(in_8), .carry_in(in_9),
    .led_a(u_sum7sec_hex_led_a), .led_b(u_sum7sec_hex_led_b), .led_c(u_sum7sec_hex_led_c),
    .led_d(u_sum7sec_hex_led_d), .led_e(u_sum7sec_hex_led_e), .led_f(u_sum7sec_hex_led_f),
    .led_g(u_sum7sec_hex_led_g), .led_h(u_sum7sec_hex_led_h));
  Seven_Seg #(.commonConnectionType("anode"), .commonCathode("true")) seven_seg_1 (
    .a(u_sum7sec_hex_led_a), .b(u_sum7sec_hex_led_b), .c(u_sum7sec_hex_led_c), .d(u_sum7sec_hex_led_d),
    .e(u_sum7sec_hex_led_e), .f(u_sum7sec_hex_led_f), .g(u_sum7sec_hex_led_g), .dp(u_sum7sec_hex_led_h),
    .common(1'b1));
endmodule
