// Digital circuit sum_7seg.dig as structural Verilog
module sum_7seg (
  input  a0,
  input  a2,
  input  a1,
  input  a3,
  input  b0,
  input  b1,
  input  b2,
  input  b3,
  input  Cin
);

  wire not_1_out, u_bcd7seg_hex_a, u_bcd7seg_hex_b, u_bcd7seg_hex_c, u_bcd7seg_hex_d, u_bcd7seg_hex_e,
       u_bcd7seg_hex_f, u_bcd7seg_hex_g, u_sum_2_cout, u_sum_2_s, u_sum_3_cout, u_sum_3_s, u_sum_4_cout,
       u_sum_4_s, u_sum_cout, u_sum_s;

  sum #(.applicationType("IVERILOG"), .CodeFile("/home/alejandro/Documents/gits/Digital-UN-2023_2/lab_sum/sum.v")) u_sum (
    .B(b0), .A(a0), .Cin(Cin), .Cout(u_sum_cout), .S(u_sum_s));
  sum #(.applicationType("IVERILOG"), .CodeFile("/home/alejandro/Documents/gits/Digital-UN-2023_2/lab_sum/sum.v")) u_sum_2 (
    .B(b1), .A(a1), .Cin(u_sum_cout), .Cout(u_sum_2_cout), .S(u_sum_2_s));
  sum #(.applicationType("IVERILOG"), .CodeFile("/home/alejandro/Documents/gits/Digital-UN-2023_2/lab_sum/sum.v")) u_sum_3 (
    .B(b2), .A(a2), .Cin(u_sum_2_cout), .Cout(u_sum_3_cout), .S(u_sum_3_s));
  sum #(.applicationType("IVERILOG"), .CodeFile("/home/alejandro/Documents/gits/Digital-UN-2023_2/lab_sum/sum.v")) u_sum_4 (
    .B(b3), .A(a3), .Cin(u_sum_3_cout), .Cout(u_sum_4_cout), .S(u_sum_4_s));
  bcd7seg_hex #(.applicationType("IVERILOG"), .CodeFile("/home/alejandro/Documents/gits/Digital-UN-2023_2/lab_sum/bcd7seg_hex.v")) u_bcd7seg_hex (
    .a1(u_sum_4_s), .b1(u_sum_3_s), .c1(u_sum_2_s), .d1(u_sum_s), .a(u_bcd7seg_hex_a), .b(u_bcd7seg_hex_b),
    .c(u_bcd7seg_hex_c), .d(u_bcd7seg_hex_d), .e(u_bcd7seg_hex_e), .f(u_bcd7seg_hex_f), .g(u_bcd7seg_hex_g));
  not not_1 (not_1_out, u_sum_4_cout);
  Seven_Seg #(.commonCathode("true"), .commonConnectionType("anode")) seven_seg_1 (
    .a(u_bcd7seg_hex_a), .b(u_bcd7seg_hex_b), .c(u_bcd7seg_hex_c), .d(u_bcd7seg_hex_d), .e(u_bcd7seg_hex_e),
    .f(u_bcd7seg_hex_f), .g(u_bcd7seg_hex_g), .dp(not_1_out), .common(1'b1));
endmodule
