// Digital circuit full_sumres.dig as structural Verilog
module full_sumres (
  input  a0,
  input  a2,
  input  a1,
  input  a3,
  input  b0,
  input  b1,
  input  b2,
  input  b3,
  input  c_in,
  input  op,
  output s0,
  output s1,
  output s2,
  output s3,
  output Cout
);

  wire u_sumres_2_cout, u_sumres_3_cout, u_sumres_cout;

  sumres #(.applicationType("IVERILOG"), .CodeFile("/home/alejandro/Documents/gits/Digital-UN-2023_2/lab_sum/sum_res_carry/sumres.v")) u_sumres (
    .a(a0), .b(b0), .c_in(c_in), .op(op), .s(s0), .cout(u_sumres_cout));
  sumres #(.applicationType("IVERILOG"), .CodeFile("/home/alejandro/Documents/gits/Digital-UN-2023_2/lab_sum/sum_res_carry/sumres.v")) u_sumres_2 (
    .a(a1), .b(b1), .c_in(u_sumres_cout), .op(op), .s(s1), .cout(u_sumres_2_cout));
  sumres #(.applicationType("IVERILOG"), .CodeFile("/home/alejandro/Documents/gits/Digital-UN-2023_2/lab_sum/sum_res_carry/sumres.v")) u_sumres_3 (
    .a(a2), .b(b2), .c_in(u_sumres_2_cout), .op(op), .s(s2), .cout(u_sumres_3_cout));
  sumres #(.applicationType("IVERILOG"), .CodeFile("/home/alejandro/Documents/gits/Digital-UN-2023_2/lab_sum/sum_res_carry/sumres.v")) u_sumres_4 (
    .a(a3), .b(b3), .c_in(u_sumres_3_cout), .op(op), .s(s3), .cout(Cout));
endmodule
