// Digital circuit sum raro.dig as structural Verilog
module sum_raro (
  input  [3:0] a,
  input  [3:0] b,
  input  carry,
  input  op,
  output [3:0] out_5,
  output out_6
);

  full_sumres #(.applicationType("IVERILOG"), .CodeFile("/home/alejandro/Documents/gits/Digital-UN-2023_2/lab_sum/sum_res_carry/full_sumres.v")) u_full_sumres (
    .in_a(a), .in_b(b), .op(carry), .out_cy0(out_6), .out_s2(out_5));
endmodule
