// Digital circuit sumres.dig as structural Verilog
module sumres (
  input  a,
  input  b,
  input  c_b_in,
  input  op,
  output s_d,
  output c_b_out
);

  wire and_1_out, and_2_out, or_1_out, xor_1_out, xor_2_out;

  xor xor_1 (xor_1_out, a, op);
  or or_1 (or_1_out, xor_1_out, b);
  xor xor_2 (xor_2_out, a, b);
  and and_1 (and_1_out, xor_1_out, b);
  and and_2 (and_2_out, or_1_out, c_b_in);
  xor xor_3 (s_d, xor_2_out, c_b_in);
  or or_2 (c_b_out, and_1_out, and_2_out);
endmodule
