// Digital circuit sumres_test.dig as structural Verilog
module sumres_test (
  input  [3:0] in_1,
  input  [3:0] in_2,
  input  in_3,
  input  clk,
  input  [1:0] in_5
);

  wire demultiplexer_1_out_0, demultiplexer_1_out_1, signo, u_clk10hz_clk_out, u_deco_7seg_a, u_deco_7seg_b,
       u_deco_7seg_c, u_deco_7seg_d, u_deco_7seg_e, u_deco_7seg_f, u_deco_7seg_g, u_full_sumres_out_cy0;
  wire [1:0] u_bin_2_bcd_d;
  wire [3:0] multiplexer_1_out, u_bin_2_bcd_u, u_full_sumres_out_s2;

  full_sumres #(.applicationType("IVERILOG"), .CodeFile("/home/alejandro/Documents/gits/Digital-UN-2023_2/lab_sum/sum_res_carry/full_sumres.v")) u_full_sumres (
    .in_a(in_1), .in_b(in_2), .op(in_3), .out_cy0(u_full_sumres_out_cy0), .out_s2(u_full_sumres_out_s2),
    .sign0(signo));
  clk10hz #(.applicationType("IVERILOG"), .CodeFile("/home/alejandro/Documents/gits/Digital-UN-2023_2/lab_sum/sum_res_carry/divi/divi.v")) u_clk10hz (
    .clk_in(clk), .clk_out(u_clk10hz_clk_out));
  // Probe on u_full_sumres_out_cy0
  // Probe on u_full_sumres_out_s2
  bin_2_bcd #(.applicationType("IVERILOG"), .CodeFile("/home/alejandro/Documents/gits/Digital-UN-2023_2/lab_sum/sum_res_carry/bin_2_bcd.v")) u_bin_2_bcd (
    .carryout(u_full_sumres_out_cy0), .out(u_full_sumres_out_s2), .d(u_bin_2_bcd_d), .u(u_bin_2_bcd_u));
  Multiplexer #(.Bits(4)) multiplexer_1 (
    .sel(u_clk10hz_clk_out), .in_0({in_5, u_bin_2_bcd_d}), .in_1(u_bin_2_bcd_u), .out(multiplexer_1_out));
  deco_7seg #(.applicationType("IVERILOG"), .CodeFile("/home/alejandro/Documents/gits/Digital-UN-2023_2/lab_sum/sum_res_carry/deco_7seg.v")) u_deco_7seg (
    .v(multiplexer_1_out), .a(u_deco_7seg_a), .b(u_deco_7seg_b), .c(u_deco_7seg_c), .d(u_deco_7seg_d),
    .e(u_deco_7seg_e), .f(u_deco_7seg_f), .g(u_deco_7seg_g));
  Demultiplexer demultiplexer_1 (
    .sel(u_clk10hz_clk_out), .in(1'b1), .out_0(demultiplexer_1_out_0), .out_1(demultiplexer_1_out_1));
  Seven_Seg #(.commonCathode("true"), .commonConnectionType("anode")) seven_seg_1 (
    .a(u_deco_7seg_a), .b(u_deco_7seg_b), .c(u_deco_7seg_c), .d(u_deco_7seg_d), .e(u_deco_7seg_e),
    .f(u_deco_7seg_f), .g(u_deco_7seg_g), .dp(signo), .common(demultiplexer_1_out_0));
  Seven_Seg #(.commonCathode("true"), .commonConnectionType("anode")) seven_seg_2 (
    .a(u_deco_7seg_a), .b(u_deco_7seg_b), .c(u_deco_7seg_c), .d(u_deco_7seg_d), .e(u_deco_7seg_e),
    .f(u_deco_7seg_f), .g(u_deco_7seg_g), .dp(signo), .common(demultiplexer_1_out_1));

  // Notes on the sheet:
  //   clk: Hz: 50000000
endmodule
